// Logisim project Proj 1.circ as structural Verilog: 4 circuits, main circuit main
module main (
  input  [7:0] in_1,
  input  in_2,
  input  in_3,
  input  in_4,
  input  [31:0] in_5,
  input  in_6,
  input  [4:0] in_7,
  input  [4:0] in_8,
  output [7:0] out_9,
  output out_10,
  output [31:0] out_11
);

  wire clock_1_out, clock_2_out;
  wire [7:0] register_1_q;
  wire [31:0] registerfile_1_p7, registerfile_1_p8;

  Clock clock_1 (.out(clock_1_out));
  Multiplexer multiplexer_1 (.in0(in_2), .in1(in_3), .out(out_10), .sel(in_4), .en(clock_1_out));
  Register register_1 (.D(in_1), .Q(register_1_q), .clk(clock_1_out));  // open: en, clr
  Register register_2 (.D(register_1_q), .Q(out_9), .clk(clock_1_out));  // open: en, clr
  // MIPSProgramROM mipsprogramrom_1: pin names not known; wires that end beside it: clock_1_out
  Clock clock_2 (.out(clock_2_out));
  // RegisterFile registerfile_1: pin names not known; wires that end beside it: in_5, clock_2_out, in_6, in_7, in_8, out_11, registerfile_1_p7, registerfile_1_p8
  Multiplexer #(.width(32)) multiplexer_2 (.in0(registerfile_1_p7), .in1(registerfile_1_p8));  // open: out, sel, en
  // MIPSProgramROM mipsprogramrom_2: pin names not known
endmodule

module Count__1 (
  input  [31:0] PC,
  output [31:0] PC_4
);

  // Incrementer incrementer_1: pin names not known; wires that end beside it: PC[31:2], PC_4[31:2]

  assign PC_4[1:0] = PC[1:0];
endmodule

module Decoder (
  input  [31:0] Op,
  output [5:0] func,
  output [4:0] shamt,
  output [4:0] rd,
  output [4:0] rt,
  output [4:0] rs,
  output Write_Enable_Register,
  output Immediate
);

  wire nand_1_out, nor_1_out, nor_2_out, not_1_out, not_2_out, not_3_out;

  not not_1 (not_1_out, Op[27]);
  not not_2 (not_2_out, Op[30]);
  nor nor_1 (nor_1_out, Op[28], Op[26], Op[27], Op[29], Op[30], Op[31]);
  nor nor_2 (nor_2_out, not_1_out, Op[28], Op[29], Op[30], Op[31]);
  nand nand_1 (nand_1_out, Op[29], not_2_out, Op[31]);
  not not_3 (not_3_out, nor_2_out);
  nor nor_3 (Immediate, nor_1_out, nor_2_out);
  and and_1 (Write_Enable_Register, not_3_out, nand_1_out);

  assign func = Op[5:0];
  assign rd = Op[15:11];
  assign rs = Op[25:21];
  assign rt = Op[20:16];
  assign shamt = Op[10:6];

  // Notes on the sheet:
  //   J Type
  //   R Type
  //   I Type
endmodule

module Isolator_2_3 (
  input  [31:0] PC_in,
  input  [15:0] Imm_in,
  input  clock,
  input  [4:0] A_in,
  input  [4:0] B_in,
  input  [4:0] rd_in,
  input  [4:0] sa_in,
  input  [3:0] op_in,
  input  WER_in,
  input  IE_in,
  input  WED_in,
  output [31:0] PC_out,
  output [15:0] Imm_out,
  output [4:0] A_out,
  output [4:0] B_out,
  output [4:0] rd_out,
  output [4:0] sa_out,
  output [3:0] op_out,
  output WER_out,
  output IE_out,
  output WED_out
);

  Register #(.width(32)) PC (.D(PC_in), .Q(PC_out), .clk(clock));  // open: en, clr
  Register #(.width(16)) Imm (.D(Imm_in), .Q(Imm_out), .clk(clock));  // open: en, clr
  Register #(.width(5)) A (.D(A_in), .Q(A_out), .clk(clock));  // open: en, clr
  Register #(.width(5)) B (.D(B_in), .Q(B_out), .clk(clock));  // open: en, clr
  Register #(.width(5)) rd (.D(rd_in), .Q(rd_out), .clk(clock));  // open: en, clr
  Register #(.width(5)) sa (.D(sa_in), .Q(sa_out), .clk(clock));  // open: en, clr
  Register #(.width(4)) aluop (.Q(op_out), .clk(clock));  // open: D, en, clr
  Register #(.width(1)) WER (.D(WER_in), .Q(WER_out), .clk(clock));  // open: en, clr
  Register #(.width(1)) IE (.D(IE_in), .Q(IE_out), .clk(clock));  // open: en, clr
  Register #(.width(1)) WED (.D(WED_in), .Q(WED_out), .clk(clock));  // open: en, clr
endmodule
